# Fritzing sketch gameFritzing (saved by Fritzing 1.0.4)
breadboards: 2

parts:
  Part1 = Arduino Uno (Rev3) - ICSP
  Buzzer = Piezo Speaker
  R1 = Resistor [tolerance=±5% power=0.25W resistance=220 package=THT]
  S1 = Pushbutton [package="[THT]"]
  S2 = Pushbutton [package="[THT]"]
  S3 = Pushbutton [package="[THT]"]
  S4 = Pushbutton [package="[THT]"]
  S5 = Pushbutton [package="[THT]"]
  LED1 = LED - 5mm [color="Red (633nm)" current=0.030A package="5 mm [THT]"]
  LED2 = LED - 5mm [color="Green (570nm)" current=0.030A package="5 mm [THT]"]
  LED3 = LED - 5mm [color="Yellow (595nm)" current=0.030A package="5 mm [THT]"]
  LED4 = LED - 5mm [color="Blue (525nm)" current=0.030A package="5 mm [THT]"]
  R2 = Resistor [tolerance=±5% power=0.25W resistance=220 package=THT]
  R3 = Resistor [tolerance=±5% power=0.25W resistance=220 package=THT]
  R4 = Resistor [tolerance=±5% power=0.25W resistance=220 package=THT]
  R5 = Resistor [tolerance=±5% power=0.25W resistance=220 package=THT]

nets:
  N1: Part1.A0, R1.Pin_1
  N2: Part1.A1, R2.Pin_0
  N3: Part1.A2, R3.Pin_0
  N4: Part1.A3, R4.Pin_0
  N5: Part1.A4/SDA, R5.Pin_0
  N6: Part1.GND, Part1.D2, Part1.D3_PWM, Part1.D4, Part1.D5_PWM, Buzzer.pin1, S1.Pin_3, S1.Pin_4, S2.Pin_3, S2.Pin_4, S3.Pin_3, S3.Pin_4, S4.Pin_3, S4.Pin_4, S5.Pin_1, S5.Pin_2, LED1.cathode, LED2.cathode, LED3.cathode, LED4.cathode
  N7: Part1.D6_PWM, S5.Pin_3, S5.Pin_4
  N8: Buzzer.pin2, R1.Pin_0
  N9: S1.Pin_1, S1.Pin_2
  N10: S2.Pin_1, S2.Pin_2
  N11: S3.Pin_1, S3.Pin_2
  N12: S4.Pin_1, S4.Pin_2
  N13: LED1.anode, R2.Pin_1
  N14: LED2.anode, R3.Pin_1
  N15: LED3.anode, R4.Pin_1
  N16: LED4.anode, R5.Pin_1
